// Logisim project design.circ as structural Verilog: 1 circuit, main circuit main
module main (
);

  wire buffer_1_out, buffer_2_out, Clock_out, decoder_1_out0, decoder_1_out1, decoder_1_out2, decoder_1_out3,
       decoder_3_out0, decoder_3_out1, decoder_3_out2, decoder_3_out3, decoder_3_out4, decoder_3_out5,
       decoder_3_out6, decoder_3_out7, decoder_3_out8, not_1_out, not_2_out, or_1_out, or_2_out, Reset_out;
  wire [1:0] adder_2_out, Step_q;
  wire [3:0] undriven;
  wire [31:0] A_register_q, adder_1_out, adder_3_out, adder_4_out, and_1_out, B_register_q, C_register_q,
       D_register_q, divider_1_out, divider_1_rem, E_register_q, F_register_q, G_register_q, H_register_q,
       Instruction_byte_1_q, Instruction_byte_2_q, Instruction_Pointer_q, multiplexer_1_out,
       multiplexer_2_out, multiplexer_3_out, multiplexer_4_out, multiplier_1_out, not_3_out, or_3_out,
       rom_1_data, shifter_1_out, shifter_2_out, shifter_3_out, shifter_4_out, xor_1_out, Z_register_q;

  Adder #(.width(32)) adder_1 (.a(Instruction_Pointer_q), .b(32'h4), .out(adder_1_out));  // open: cin, cout
  Multiplexer #(.width(32), .enable("false")) multiplexer_1 (
    .in0(adder_1_out), .in1(32'h80000000), .out(multiplexer_1_out), .sel(Reset_out));
  Button Reset (.out(Reset_out));
  Clock Clock (.out(Clock_out));
  Adder #(.width(2)) adder_2 (.a(Step_q), .b(2'b01), .out(adder_2_out));  // open: cin, cout
  Register #(.width(32)) Instruction_Pointer (
    .D(multiplexer_1_out), .en(not_1_out), .Q(Instruction_Pointer_q), .clk(or_1_out));  // open: clr
  not not_1 (not_1_out, decoder_1_out2);
  or or_1 (or_1_out, Clock_out, buffer_1_out);
  buf buffer_1 (buffer_1_out, buffer_2_out);
  buf buffer_2 (buffer_2_out, Reset_out);
  Register #(.width(2)) Step (.D(adder_2_out), .Q(Step_q), .clk(Clock_out), .clr(or_2_out));  // open: en
  or or_2 (or_2_out, Reset_out, decoder_1_out3);
  Decoder #(.select(2), .disabled(0), .enable("false")) decoder_1 (
    .out0(decoder_1_out0), .out1(decoder_1_out1), .out2(decoder_1_out2), .out3(decoder_1_out3), .sel(Step_q));
  not not_2 (not_2_out, Instruction_Pointer_q[31]);
  ROM #(.addrWidth(24), .dataWidth(32)) rom_1 (
    .addr(Instruction_Pointer_q[25:2]), .data(rom_1_data), .sel(Instruction_Pointer_q[31]));
  RAM #(.addrWidth(24), .dataWidth(32)) ram_1 (
    .addr(Instruction_Pointer_q[25:2]), .data(rom_1_data), .sel(not_2_out), .clk(Clock_out), .clr(Reset_out));  // open: ld
  Register #(.width(32)) Instruction_byte_1 (
    .D(rom_1_data), .en(decoder_1_out0), .Q(Instruction_byte_1_q), .clk(Clock_out), .clr(Reset_out));
  Register #(.width(32)) Instruction_byte_2 (
    .D(rom_1_data), .en(decoder_1_out1), .Q(Instruction_byte_2_q), .clk(Clock_out), .clr(Reset_out));
  Decoder #(.select(5)) decoder_2 (
    .sel(Instruction_byte_1_q[4:0]), .en(decoder_1_out2));  // open: out0, out1, out2, out3, out4, out5, out6, out7, out8, out9, out10, out11, out12, out13, out14, out15, out16, out17, out18, out19, out20, out21, out22, out23, out24, out25, out26, out27, out28, out29, out30, out31
  Adder #(.width(32)) adder_3 (
    .a(multiplexer_3_out), .b({Instruction_byte_2_q[23:0], Instruction_byte_1_q[31:24]}), .out(adder_3_out));  // open: cin, cout
  assign and_1_out = multiplexer_4_out & adder_3_out;  // AND_Gate and_1, 32 bits wide
  assign or_3_out = multiplexer_4_out | adder_3_out;  // OR_Gate or_3, 32 bits wide
  assign not_3_out = ~adder_3_out;  // NOT_Gate not_3, 32 bits wide
  Adder #(.width(32)) adder_4 (.a(multiplexer_4_out), .b(adder_3_out), .out(adder_4_out));  // open: cin, cout
  assign xor_1_out = multiplexer_4_out ^ adder_3_out;  // XOR_Gate xor_1, 32 bits wide
  Shifter #(.width(32)) shifter_1 (.in(multiplexer_4_out), .\dist (adder_3_out[4:0]), .out(shifter_1_out));
  Shifter #(.width(32), .shift("lr")) shifter_2 (
    .in(multiplexer_4_out), .\dist (adder_3_out[4:0]), .out(shifter_2_out));
  Shifter #(.width(32), .shift("rl")) shifter_3 (
    .in(multiplexer_4_out), .\dist (adder_3_out[4:0]), .out(shifter_3_out));
  Shifter #(.width(32), .shift("rr")) shifter_4 (
    .in(multiplexer_4_out), .\dist (adder_3_out[4:0]), .out(shifter_4_out));
  Multiplier #(.width(32)) multiplier_1 (
    .a(multiplexer_4_out), .b(adder_3_out), .out(multiplier_1_out));  // open: cin, cout
  Divider #(.width(32)) divider_1 (
    .a(multiplexer_4_out), .b(adder_3_out), .out(divider_1_out), .rem(divider_1_rem));  // open: upper
  Multiplexer #(.select(4), .width(32), .enable("false")) multiplexer_2 (
    .in0(adder_3_out), .in1(adder_4_out), .in2(and_1_out), .in3(or_3_out), .in4(xor_1_out), .in5(not_3_out),
    .in6(shifter_1_out), .in7(shifter_2_out), .in8(shifter_3_out), .in9(shifter_4_out),
    .in10(multiplier_1_out), .in11(divider_1_out), .in12(divider_1_rem), .out(multiplexer_2_out),
    .sel(undriven));  // open: in13, in14, in15
  Decoder #(.select(4), .disabled(0), .enable("false")) decoder_3 (
    .out0(decoder_3_out0), .out1(decoder_3_out1), .out2(decoder_3_out2), .out3(decoder_3_out3),
    .out4(decoder_3_out4), .out5(decoder_3_out5), .out6(decoder_3_out6), .out7(decoder_3_out7),
    .out8(decoder_3_out8), .sel(Instruction_byte_1_q[19:16]));  // open: out9, out10, out11, out12, out13, out14, out15
  Register #(.width(32)) Z_register (
    .D(multiplexer_2_out), .en(decoder_3_out0), .Q(Z_register_q), .clk(Reset_out), .clr(Clock_out));
  Register #(.width(32)) D_register (
    .D(multiplexer_2_out), .en(decoder_3_out4), .Q(D_register_q), .clk(Reset_out), .clr(Clock_out));
  Register #(.width(32)) H_register (
    .D(multiplexer_2_out), .en(decoder_3_out8), .Q(H_register_q), .clk(Clock_out), .clr(Reset_out));
  Register #(.width(32)) A_register (
    .D(multiplexer_2_out), .en(decoder_3_out1), .Q(A_register_q), .clk(Reset_out), .clr(Clock_out));
  Register #(.width(32)) E_register (
    .D(multiplexer_2_out), .en(decoder_3_out5), .Q(E_register_q), .clk(Reset_out), .clr(Clock_out));
  Register #(.width(32)) B_register (
    .D(multiplexer_2_out), .en(decoder_3_out2), .Q(B_register_q), .clk(Reset_out), .clr(Clock_out));
  Register #(.width(32)) F_register (
    .D(multiplexer_2_out), .en(decoder_3_out6), .Q(F_register_q), .clk(Reset_out), .clr(Clock_out));
  Register #(.width(32)) C_register (
    .D(multiplexer_2_out), .en(decoder_3_out3), .Q(C_register_q), .clk(Reset_out), .clr(Clock_out));
  Register #(.width(32)) G_register (
    .D(multiplexer_2_out), .en(decoder_3_out7), .Q(G_register_q), .clk(Reset_out), .clr(Clock_out));
  Multiplexer #(.select(4), .width(32), .enable("false")) multiplexer_3 (
    .in0(Z_register_q), .in1(A_register_q), .in2(B_register_q), .in3(C_register_q), .in4(D_register_q),
    .in5(E_register_q), .in6(F_register_q), .in7(G_register_q), .in8(H_register_q), .out(multiplexer_3_out),
    .sel(Instruction_byte_1_q[23:20]));  // open: in9, in10, in11, in12, in13, in14, in15
  Multiplexer #(.select(4), .width(32), .enable("false")) multiplexer_4 (
    .in0(Z_register_q), .in1(A_register_q), .in2(B_register_q), .in3(C_register_q), .in4(D_register_q),
    .in5(E_register_q), .in6(F_register_q), .in7(G_register_q), .in8(H_register_q), .out(multiplexer_4_out),
    .sel(Instruction_byte_1_q[19:16]));  // open: in9, in10, in11, in12, in13, in14, in15

  // Notes on the sheet:
  //   Destination
  //   Source
  //   Destination
endmodule
